# Fritzing sketch ADC0832 (saved by Fritzing 0.9.3b)
breadboards: 1

parts:
  0832 = DIP - 8 pins [package="DIP (Dual Inline) [THT]"]
  Raspberry_Pi_1 = Raspberry Pi 3 [part_number=RPI-3-V1.2]
  R1 = Rotary Potentiometer (Small) [maximum_resistance=100kΩ package=THT]

nets:
  N1: 0832.CS, Raspberry_Pi_1.GPIO21
  N2: 0832.CH0, R1.wiper
  N3: 0832.pin4, 0832.pin8, Raspberry_Pi_1.5V, R1.leg1, R1.leg2
  N4: 0832.pin5, 0832.pin6, Raspberry_Pi_1.GPIO16
  N5: 0832.pin7, Raspberry_Pi_1.GPIO20

custom parts:
  DIP - 8 pins: A DIP stand-in part for whatever IC you want. With 8 pins on a 300mil dual inline package (DIP) footprint.
